// Logisim project PC.circ as structural Verilog: 1 circuit, main circuit main
module main (
  input  [15:0] Input,
  input  Load,
  input  Inc,
  input  Reset,
  output [15:0] Out
);

  // Register register_1: pin names not known
endmodule
